# Fritzing sketch STC-1000 ESP8266 DataLogger Final 151221 (saved by Fritzing 0.9.2b)
circuit board: 8.46667cm x 5.64444cm
breadboards: 1

parts:
  Part1 = HUZZAH ESP8266 Breakout
  OLED1 = 128x64 Monochrom OLED Display with SPI Control
  R1 = Resistor [tolerance=±5% resistance=10k package=THT]
  D1 = Schottky Diode [part_number=1N5817 package="300 mil [THT]"]
  USB_Micro-B = mystery part, 5 pins [chip_label="USB MicroB"]
  STC-1000_Pgm_Header = Generic male header - 5 pins [form="♂ (male)" package=THT]
  R3 = Resistor [tolerance=±1% resistance=3.9k package=THT]
  R2 = Resistor [tolerance=±1% resistance=7.5k package=THT]

nets:
  GND: Part1.GND, OLED1.GND, R1.Pin_0, USB_Micro-B.pin1, STC-1000_Pgm_Header.GND, R3.Pin_1
  N1: Part1.GPIO16, OLED1.Reset
  N2: Part1.GPIO14, OLED1.Clock
  N3: Part1.GPIO13, OLED1.Data
  N4: Part1.VIN, USB_Micro-B.pin5
  3.3V: Part1.3.3V, OLED1.3v3, D1.anode
  N5: Part1.GPIO15, OLED1.CS
  N6: Part1.GPIO2, OLED1.SA0/DC
  N7: Part1.GPIO5, R3.Pin_0, R2.Pin_1
  N8: R1.Pin_1, STC-1000_Pgm_Header.ICSPDAT, R2.Pin_0
  N9: D1.cathode, STC-1000_Pgm_Header.VDD

notes:
  Data Logger for STC-1000+ w/ OLED

custom parts:
  HUZZAH ESP8266 Breakout: The ESP8266 processor from Espressif is an 80 MHz microcontroller with a full WiFi front-end (both as client and access point) and TCP/IP stack with DNS support as well.
  Generic male header - 5 pins: Generic male header
